# Fritzing sketch DifferentialOpAmp (saved by Fritzing 0.9.3b)
breadboards: 1

parts:
  Part1 = Arduino Mega 2560 (Rev3)
  R3 = Resistor [tolerance=±5% resistance=10k package=THT]
  R5 = Resistor [tolerance=±5% resistance=10k package=THT]
  R6 = Photocell (LDR) [package=THT]
  U1 = LM 358 Dual Op-Amp [package="DIP8 [THT]"]
  R7 = Resistor [tolerance=±5% resistance=1k package=THT]
  R8 = Resistor [tolerance=±5% resistance=2k package=THT]
  R9 = Resistor [tolerance=±5% resistance=2k package=THT]
  R10 = Resistor [tolerance=±5% resistance=660 package=THT]
  Q1 = NPN-Transistor [package="SOT-23 [SMD]"]
  R11 = Resistor [tolerance=±5% resistance=1k package=THT]
  R12 = Resistor [tolerance=±5% resistance=220 package=THT]
  LED1 = LED - 5mm [color="Red (633nm)" package="5 mm [THT]"]

nets:
  N1: Part1.GND, R6.pin_1, U1.connector3, Q1.1
  N2: Part1.5V, R3.Pin_0, R5.Pin_0, U1.connector7, R12.Pin_0
  N3: R3.Pin_1, R6.pin_0, U1.connector2
  N4: R5.Pin_1, R7.Pin_0, R8.Pin_0, R9.Pin_0
  N5: U1.connector0, R10.Pin_1, R11.Pin_0
  N6: U1.connector1, R7.Pin_1
  N7: R8.Pin_1, R10.Pin_0
  N8: Q1.2, LED1.anode
  N9: Q1.0, R11.Pin_1
  N10: R12.Pin_1, LED1.cathode
