# Fritzing sketch Greenhouse (saved by Fritzing 0.9.3b)
breadboards: 2

parts:
  Part1 = Arduino Mega 2560 (Rev3)
  Part2 = Arduino Uno (Rev3)
  LED1 = LED - 5mm [color="Red (633nm)" package="5 mm [THT]"]
  LED2 = LED - 5mm [color="Red (633nm)" package="5 mm [THT]"]
  LED3 = LED - 5mm [color="Red (633nm)" package="5 mm [THT]"]
  LED4 = LED - 5mm [color="Red (633nm)" package="5 mm [THT]"]
  LED5 = LED - 5mm [color="Red (633nm)" package="5 mm [THT]"]
  J1 = Piezo Speaker
  R1 = Resistor [tolerance=±5% resistance=220 package=THT]
  J2 = Piezo Speaker
  R2 = Photocell (LDR) [package=THT]
  R3 = Photocell (LDR) [package=THT]
  LED6 = LED - 5mm [color="Red (633nm)" package="5 mm [THT]"]
  R4 = Resistor [tolerance=±5% resistance=220 package=THT]
  R5 = Resistor [tolerance=±5% resistance=220 package=THT]
  R6 = Resistor [tolerance=±5% resistance=220 package=THT]
  R7 = Resistor [tolerance=±5% resistance=220 package=THT]
  LED7 = RGB LED (com. cathode, rgb) [package="5 mm [THT]"]
  R8 = Resistor [tolerance=±5% resistance=220 package=THT]
  R9 = Resistor [tolerance=±5% resistance=220 package=THT]
  R10 = Resistor [tolerance=±5% resistance=220 package=THT]
  J3 = Infrared Proximity Sensor  # not connected

nets:
  N1: Part1.A0, R3.pin_1, R5.Pin_0
  N2: Part1.A3, R2.pin_1, R6.Pin_0
  N3: Part1.D11_PWM, J2.pin2
  N4: Part1.D8_PWM, LED6.cathode
  N5: Part1.5V, R2.pin_0, R3.pin_0, LED7.common_cathode
  N6: Part1.GND, R4.Pin_1, R5.Pin_1, R6.Pin_1, R7.Pin_0
  N7: Part1.D2_PWM, R8.Pin_0
  N8: Part1.D4_PWM, R9.Pin_1
  N9: Part1.D6_PWM, R10.Pin_1
  N10: Part2.D9_PWM, LED2.cathode
  N11: Part2.D10_PWM/SS, LED1.cathode
  N12: Part2.D11_PWM/MOSI, R1.Pin_0
  N13: Part2.D3_PWM, LED5.cathode
  N14: Part2.D5_PWM, LED4.cathode
  N15: Part2.D6_PWM, LED3.cathode
  N16: Part2.GND, LED1.anode, LED2.anode, LED3.anode, LED4.anode, LED5.anode, J1.pin1
  N17: J1.pin2, R1.Pin_1
  N18: J2.pin1, R7.Pin_1
  N19: LED6.anode, R4.Pin_0
  N20: LED7.red_anode, R8.Pin_1
  N21: LED7.green_anode, R9.Pin_0
  N22: LED7.blue_anode, R10.Pin_0
