# Fritzing sketch LEDlight (saved by Fritzing 0.9.3b)
breadboards: 1

parts:
  Part1 = Arduino Mega 2560 (Rev3)
  LED1 = RGB LED (com. cathode, rgb) [package="5 mm [THT]"]
  R1 = Photocell (LDR) [package=THT]
  R2 = Resistor [tolerance=±5% resistance=220 package=THT]
  R3 = Resistor [tolerance=±5% resistance=220 package=THT]
  R4 = Resistor [tolerance=±5% resistance=220 package=THT]
  R5 = Resistor [tolerance=±5% resistance=220 package=THT]

nets:
  N1: Part1.A0, R1.pin_1, R2.Pin_0
  N2: Part1.5V, LED1.common_cathode, R1.pin_0
  N3: Part1.GND, R2.Pin_1
  N4: Part1.D2_PWM, R5.Pin_1
  N5: Part1.D4_PWM, R4.Pin_1
  N6: Part1.D6_PWM, R3.Pin_0
  N7: LED1.red_anode, R3.Pin_1
  N8: LED1.green_anode, R4.Pin_0
  N9: LED1.blue_anode, R5.Pin_0

notes:
  Zachary Scherer
