# Fritzing sketch LightLadderSpeaker (saved by Fritzing 0.9.3b)
breadboards: 1

parts:
  Part1 = Arduino Uno (Rev3)
  LED1 = LED - 5mm [color="Red (633nm)" package="5 mm [THT]"]
  LED2 = LED - 5mm [color="Red (633nm)" package="5 mm [THT]"]
  LED3 = LED - 5mm [color="Red (633nm)" package="5 mm [THT]"]
  LED4 = LED - 5mm [color="Red (633nm)" package="5 mm [THT]"]
  LED5 = LED - 5mm [color="Red (633nm)" package="5 mm [THT]"]
  J1 = Piezo Speaker
  R1 = Resistor [tolerance=±5% resistance=200 package=THT]

nets:
  N1: Part1.D9_PWM, LED4.cathode
  N2: Part1.D10_PWM/SS, LED5.cathode
  N3: Part1.D11_PWM/MOSI, R1.Pin_1
  N4: Part1.GND, LED1.anode, LED2.anode, LED3.anode, LED4.anode, LED5.anode, J1.pin1
  N5: Part1.D3_PWM, LED1.cathode
  N6: Part1.D5_PWM, LED2.cathode
  N7: Part1.D6_PWM, LED3.cathode
  N8: J1.pin2, R1.Pin_0
