# Fritzing sketch Theramin (saved by Fritzing 0.9.3b)
breadboards: 1

parts:
  Part1 = Arduino Mega 2560 (Rev3)
  R1 = Photocell (LDR) [package=THT]
  R2 = Resistor [tolerance=±5% resistance=10k package=THT]
  J1 = Piezo Speaker
  R3 = Resistor [tolerance=±5% resistance=220 package=THT]

nets:
  N1: Part1.A3, R1.pin_1, R2.Pin_0
  N2: Part1.GND, R2.Pin_1, R3.Pin_0
  N3: Part1.D11_PWM, J1.pin2
  N4: Part1.5V, R1.pin_0
  N5: J1.pin1, R3.Pin_1
